# Fritzing sketch breadboard_example (saved by Fritzing 0.9.3b)
breadboards: 1

parts:
  IC1 = MICROCONTROLLER [package=dil28-3-simon-kit]
  XTAL1 = Crystal [frequency="16 Mhz" package=THT]
  C1 = Capacitor [package=cap-pth-small2]
  C2 = Capacitor [package=cap-pth-small2]
  C3 = Capacitor [package=cap-pth-small2]
  U1 = Voltage Regulator - 5V [package="TO220 [THT]"]
  C4 = Capacitor [package=cap-pth-small2]
  C5 = Capacitor [package=cap-pth-small2]
  VCC1 = Battery block 9V

nets:
  N1: IC1.VCC, C3.1, U1.output_voltage, C5.1
  N2: IC1.GND, C3.2
  N3: IC1.PB6(XTAL1_TOSC1), XTAL1.pin_0, C1.2
  N4: IC1.PB7(XTAL2_TOSC2), XTAL1.pin_1, C2.1
  N5: C1.1, C2.2, U1.GND, C4.1, C5.2, VCC1.-
  N6: U1.input_voltage, C4.2, VCC1.+
